# Fritzing sketch jaleometro_v1 (saved by Fritzing 0.9.3b)
breadboards: 1

parts:
  Mod2 = Heltec CubeCell Dev-Board [part_number=HTCC-AB01]
  Solar_Panel = Solar Cell
  SparkFun_Sound_Detector = Sound Detector
  U1 = Battery Holders [package=lipo-1100mAh]  # not connected

nets:
  N1: Mod2.pin1, SparkFun_Sound_Detector.ENVELOPE
  N2: Mod2.pin_11, Mod2.pin_14, Mod2.pin_18, Solar_Panel.-, SparkFun_Sound_Detector.GND
  N3: Mod2.pin_15, Solar_Panel.+
  N4: Mod2.pin_16, SparkFun_Sound_Detector.VCC

custom parts:
  Heltec CubeCell Dev-Board: CubeCell is a part of the Heltec LoRa series and incorporates a PSoC 4000 series processor and SX1262 RF transceiver with an integrated CP2102 USB to serial port interface and onboard SHT1.25 battery interface with integrated lithium battery management system, supporting direct solar panel connection. Links: Heltec CubeCell Dev-Board product page Github
  Sound Detector: Electret microphone with multiple outputs. - First output is the actual audio - Second output is the amplitude envelope - Third output is a binary "sound present" indication - high while sound is present, low otherwise. Visit sparkfun.com for more documentations.
