# Fritzing sketch jaleometro_v1_5 (saved by Fritzing 0.9.10b)

parts:
  Mod2 = Heltec CubeCell Dev-Board [part_number=HTCC-AB01]
  Solar_Panel = Solar Cell
  SparkFun_Sound_Detector = Sound Detector
  U1 = Battery Holders [package=lipo-1100mAh]
  J1 = Dagu DGServo 9g header (male) [package=THT]
  J3 = Dagu DGServo 9g header (male) [package=THT]
  J4 = Camdenboss CTB0158-2 [part_number=CTB0158-2 package=THT]
  J5 = Camdenboss CTB0158-5 [part_number=CTB0158-5 package=THT]
  Jumpers = Dagu DGServo 9g header (male) [package=THT]
  Q1 = NPN-Transistor [package="TO92 [THT]"]
  Mini_Micro_JST_2_0mm_PH = Header 2 [package=jst-2-pth]
  J7 = Camdenboss CTB0158-2 [part_number=CTB0158-2 package=THT]

nets:
  N1: Mod2.pin1, Q1.B
  N2: Mod2.pin2, Q1.C
  N3: Mod2.pin_11, Mod2.pin_14, Mod2.pin_18, J4.pin1, J5.pin1
  N4: Mod2.pin_15, J4.pin2
  N5: Mod2.pin_16, J5.pin2
  N6: Solar_Panel.+, J4.terminal_2
  N7: Solar_Panel.-, J4.terminal_1
  N8: SparkFun_Sound_Detector.AUDIO, J5.terminal_5
  N9: SparkFun_Sound_Detector.ENVELOPE, J5.terminal_4
  N10: SparkFun_Sound_Detector.GATE, J5.terminal_3
  N11: SparkFun_Sound_Detector.VCC, J5.terminal_2
  N12: SparkFun_Sound_Detector.GND, J5.terminal_1
  N13: U1.+, J7.terminal_2
  N14: U1.-, J7.terminal_1
  VCC: J1.Vcc, J3.Vcc, Jumpers.Vcc, Q1.E
  N15: J1.pulse, J5.pin4
  N16: J3.pulse, J5.pin3
  N17: J5.pin5, Jumpers.pulse
  N18: Mini_Micro_JST_2_0mm_PH.1, J7.pin2
  N19: Mini_Micro_JST_2_0mm_PH.2, J7.pin1

custom parts:
  Heltec CubeCell Dev-Board: CubeCell is a part of the Heltec LoRa series and incorporates a PSoC 4000 series processor and SX1262 RF transceiver with an integrated CP2102 USB to serial port interface and onboard SHT1.25 battery interface with integrated lithium battery management system, supporting direct solar panel connection. Links: Heltec CubeCell Dev-Board product page Github
  Sound Detector: Electret microphone with multiple outputs. - First output is the actual audio - Second output is the amplitude envelope - Third output is a binary "sound present" indication - high while sound is present, low otherwise. Visit sparkfun.com for more documentations.
