# Fritzing sketch jaleometro (saved by Fritzing 0.9.3b)

parts:
  Mod2 = Heltec CubeCell Dev-Board [part_number=HTCC-AB01]
  5V_DC = 2.1mm Barrel Jack with Terminal Block  # not connected
  Part1 = Solar Cell
  PART1 = Sound Detector
  U1 = LIPO-110mAh [package=lipo-110]  # not connected

nets:
  N1: Mod2.pin1, PART1.ENVELOPE
  N2: Mod2.pin_10, PART1.VCC
  N3: Mod2.pin_11, Mod2.pin_14, Mod2.pin_18, Part1.-, PART1.GND
  N4: Mod2.pin_15, Part1.+

custom parts:
  Heltec CubeCell Dev-Board: CubeCell is a part of the Heltec LoRa series and incorporates a PSoC 4000 series processor and SX1262 RF transceiver with an integrated CP2102 USB to serial port interface and onboard SHT1.25 battery interface with integrated lithium battery management system, supporting direct solar panel connection. Links: Heltec CubeCell Dev-Board product page Github
  Sound Detector: Electret microphone with multiple outputs. - First output is the actual audio - Second output is the amplitude envelope - Third output is a binary "sound present" indication - high while sound is present, low otherwise. Visit sparkfun.com for more documentations.
